# Fritzing sketch Untitled Sketch1 (saved by Fritzing 0.9.3b)
circuit board: 15cm x 10cm
perfboards: 1
breadboards: 3

parts:
  U1 = atmega328 [package=dip]
  IC1 = DS1307 [package=THT]
  XTAL1 = Crystal [frequency="16 Mhz" package=THT]
  C1 = Ceramic Capacitor [capacitance=22pF voltage=50V package="100 mil [THT, multilayer]"]
  C2 = Ceramic Capacitor [capacitance=100nF package="100 mil [THT, multilayer]"]
  R1 = Resistor [tolerance=±5% resistance=10k package=THT]
  BAT1 = Battery Holders [package=battcom_20mm_pth]
  Y4 = CRYSTAL [package=tc26h]
  Componente2 = NRF24L01+ Breakout Board
  IC2 = Voltage Regulator LM1117 [package=sot223]
  C3 = Electrolytic Capacitor [capacitance=10µF voltage=20V package="100 mil [THT, electrolytic]"]
  C4 = Electrolytic Capacitor [capacitance=1µF package="100 mil [THT, electrolytic]"]
  Maluska1 = maluska dil miniaturrelais [part_number="DIL Mini RY" package=THT]
  Q1 = NPN-Transistor [package="TO92 [THT]"]
  J1 = female pin header, 5 pins [form="♀ (female)"]
  J2 = female pin header, 5 pins [form="♀ (female)"]
  Bateria = Camdenboss CTB0158-2 [part_number=CTB0158-2 package=THT]
  R2 = Resistor [tolerance=±5% resistance=1k package=THT]
  U2 = Sharp PC817 [package=THT]
  R3 = Resistor [tolerance=±5% resistance=4.7k package=THT]
  R4 = Resistor [tolerance=±5% resistance=330 package=THT]
  Motor = Camdenboss CTB0158-2 [part_number=CTB0158-2 package=THT]
  D1 = Rectifier Diode [part_number=1N4001 package="300 mil [THT]"]
  LED2 = LED - 5mm [color="Green (565nm)" package="5 mm [THT]"]
  LED1 = LED - 5mm [color="Blue (505nm)" package="5 mm [THT]"]
  R7 = Resistor [tolerance=±5% resistance=220 package=THT]
  R8 = Resistor [tolerance=±5% resistance=220 package=THT]

nets:
  N1: U1.RESET, R1.Pin_0
  N2: U1.D2, U2.Pin_2, LED1.cathode
  N3: U1.VCC, U1.AVCC, IC1.+V, R1.Pin_1, IC2.IN, C3.+, J1.pin1, R4.Pin_0
  GND: U1.GND, IC1.0V, C1.1, C2.1, BAT1.-, Componente2.GND, IC2.ADJ, C3.-, C4.-, J1.pin5, LED2.cathode, R7.Pin_0, R8.Pin_0
  N4: U1.XLAT1, XTAL1.pin_0, C1.0
  N5: U1.XLAT2, XTAL1.pin_1, C2.0
  N6: U1.D9_(PWM), Componente2.CE
  N7: U1.D10_(PWM), Componente2.CS
  N8: U1.D11_(PWM), Componente2.MOSI
  N9: U1.D12, Componente2.MISO
  N10: U1.D13, Componente2.SCK
  N11: U1.A4, IC1.SDA_-_I2C_Data
  N12: U1.A5, IC1.SCL_-_I2C_Clock
  N13: IC1.X1_-_Crystal, Y4.2
  N14: IC1.X2_-_Crystal, Y4.1
  N15: IC1.Vbat_-_Backup_Supply, BAT1.+
  N16: Componente2.VCC, IC2.OUT, C4.+
  N17: Maluska1.1, Maluska1.6, Maluska1.11, J2.pin1, Bateria.pin2, R3.Pin_1, D1.cathode
  N18: Maluska1.8, Maluska1.9, Motor.pin2
  N19: Maluska1.16, Q1.C, D1.anode
  N20: Q1.E, J2.pin5, Bateria.pin1, U2.Pin_3, Motor.pin1
  N21: Q1.B, R2.Pin_1
  N22: R2.Pin_0, U2.Pin_4, R3.Pin_0
  N23: U2.Pin_1, R4.Pin_1
  N24: LED2.anode, R7.Pin_1
  N25: LED1.anode, R8.Pin_1
