# Fritzing sketch pequena (saved by Fritzing 0.9.3b)
circuit board: 8.46667cm x 5.86662cm
breadboards: 1

parts:
  Componente1 = Arduino Uno (Rev3)
  Componente2 = NRF24L01+ Breakout Board
  IC2 = DS1307 [package=THT]
  BAT2 = Battery Holders [package=battcom_20mm_pth]
  Y6 = CRYSTAL [package=tc26h]
  J1 = female pin header, 8 pins [form="♀ (female)"]
  J2 = female pin header, 6 pins [form="♀ (female)"]

nets:
  N1: Componente1.A4/SDA, IC2.SDA_-_I2C_Data
  N2: Componente1.A5/SCL, IC2.SCL_-_I2C_Clock
  N3: Componente1.D8, Componente2.CS
  N4: Componente1.D11_PWM/MOSI, Componente2.MOSI
  N5: Componente1.D12/MISO, Componente2.MISO
  N6: Componente1.D13/SCK, Componente2.SCK
  N7: Componente1.D0/RX, J1.pin1
  N8: Componente1.D1/TX, J1.pin2
  N9: Componente1.D2, J1.pin3
  N10: Componente1.D3_PWM, J1.pin4
  N11: Componente1.D4, J1.pin5
  N12: Componente1.D5_PWM, J1.pin6
  N13: Componente1.D6_PWM, J1.pin7
  N14: Componente1.D7, Componente2.CE, J1.pin8
  N15: Componente1.RESET, J2.pin1
  3V3: Componente1.3V3, Componente2.VCC, J2.pin2
  N16: Componente1.5V, IC2.+V, J2.pin3
  GND: Componente1.GND, Componente2.GND, IC2.0V, BAT2.-, J2.pin4, J2.pin5
  N17: Componente1.VIN, J2.pin6
  N18: IC2.X1_-_Crystal, Y6.2
  N19: IC2.X2_-_Crystal, Y6.1
  N20: IC2.Vbat_-_Backup_Supply, BAT2.+
