# Fritzing sketch placa completaV1 (saved by Fritzing 0.9.3b)
circuit board: 11.317cm x 16.2348cm
breadboards: 2

parts:
  U2 = atmega328 [package=dip]
  XTAL2 = Crystal [frequency="16 Mhz" package=THT]
  C3 = Ceramic Capacitor [capacitance=22pF voltage=16V package="100 mil [THT, multilayer]"]
  C4 = Ceramic Capacitor [capacitance=22pF voltage=16V package="100 mil [THT, multilayer]"]
  R2 = Resistor [tolerance=±5% resistance=10k package=THT]
  BAT2 = Battery Holders [package=battcom_20mm_pth]
  Y5 = CRYSTAL [package=tc26h]
  Componente3 = NRF24L01+ Breakout Board
  S2 = Pushbutton [package="[THT]"]
  U4 = Voltage Regulator - 3.3V [package="TO220 [THT]"]
  C7 = Tantalum Capacitor [capacitance=1μF package="100 mil [THT, tantalum]"]
  C6 = Ceramic Capacitor [capacitance=0.1µF voltage=16V package="100 mil [THT, multilayer]"]
  C8 = Electrolytic Capacitor [capacitance=1μF package="100 mil [THT, electrolytic]"]
  IC2 = DS1307 [package=THT]
  R9 = Resistor [tolerance=±5% resistance=220 package=THT]
  Q2 = NPN-Transistor [package="TO92 [THT]"]
  R10 = Resistor [tolerance=±5% resistance=1k package=THT]
  U5 = Sharp PC817 [package=THT]
  R11 = Resistor [tolerance=±5% resistance=4.7k package=THT]
  R12 = Resistor [tolerance=±5% resistance=330 package=THT]
  LED3 = LED - 5mm [color="Blue (505nm)" package="5 mm [THT]"]
  D2 = Rectifier Diode [part_number=1N4001 package="300 mil [THT]"]
  LED4 = LED - 5mm [color="Green (565nm)" package="5 mm [THT]"]
  R13 = Resistor [tolerance=±5% resistance=220 package=THT]
  C14 = Electrolytic Capacitor [capacitance=1000µF voltage=16V package="200 mil [THT, electrolytic]"]
  J14 = Camdenboss CTB0158-4 [part_number=CTB0158-4 package=THT]
  R14 = Resistor [tolerance=±5% resistance=220 package=THT]
  R15 = Resistor [tolerance=±5% resistance=220 package=THT]
  D6 = Schottky Diode [part_number=1N5817 package="300 mil [THT]"]
  OMRON1 = OMRON PCB Power Relay – G5LE [part_number="G5LE-1\n" package=THT]
  L3 = Inductor [package="400 mil [THT]"]
  L5 = Inductor [inductance=33µH package="400 mil [THT]"]
  L4 = Inductor [package="400 mil [THT]"]
  C13 = Electrolytic Capacitor [capacitance=100μF package="100 mil [THT, electrolytic]"]
  J12 = female pin header, 3 pins [form="♀ (female)"]
  J13 = female pin header, 2 pins [form="♀ (female)"]
  J26 = female pin header, 1 pin [form="♀ (female)"]
  J27 = female pin header, 1 pin [form="♀ (female)"]
  J28 = female pin header, 1 pin [form="♀ (female)"]
  J29 = female pin header, 1 pin [form="♀ (female)"]
  J30 = female pin header, 1 pin [form="♀ (female)"]
  J31 = female pin header, 1 pin [form="♀ (female)"]
  J32 = female pin header, 1 pin [form="♀ (female)"]
  J33 = female pin header, 1 pin [form="♀ (female)"]
  J34 = female pin header, 1 pin [form="♀ (female)"]
  J35 = female pin header, 1 pin [form="♀ (female)"]
  J21 = female pin header, 1 pin [form="♀ (female)"]  # not connected
  J20 = female pin header, 1 pin [form="♀ (female)"]  # not connected
  J36 = female pin header, 1 pin [form="♀ (female)"]
  J37 = female pin header, 1 pin [form="♀ (female)"]
  J38 = female pin header, 1 pin [form="♀ (female)"]
  J39 = female pin header, 1 pin [form="♀ (female)"]
  J40 = female pin header, 1 pin [form="♀ (female)"]
  J41 = female pin header, 1 pin [form="♀ (female)"]
  J42 = female pin header, 1 pin [form="♀ (female)"]
  J43 = female pin header, 1 pin [form="♀ (female)"]
  J44 = female pin header, 1 pin [form="♀ (female)"]
  J45 = female pin header, 1 pin [form="♀ (female)"]
  J47 = female pin header, 1 pin [form="♀ (female)"]
  J46 = female pin header, 1 pin [form="♀ (female)"]
  J25 = female pin header, 1 pin [form="♀ (female)"]
  J24 = female pin header, 1 pin [form="♀ (female)"]

nets:
  N1: U2.RESET, R2.Pin_0, S2.Pin_1, S2.Pin_2
  N2: U2.D2, J41.pin1
  N3: U2.D3_(PWM), J42.pin1
  N4: U2.D4, J43.pin1
  N5: U2.VCC, U2.AVCC, R2.Pin_1, U4.input_voltage, C6.0, C8.+, IC2.+V, R12.Pin_0, R13.Pin_0, C14.+, L3.pin_1, J13.pin2, J27.pin1, J29.pin1, J31.pin1, J33.pin1, J35.pin1, J38.pin1, J46.pin1
  GND: U2.GND, C3.1, C4.1, BAT2.-, Componente3.GND, S2.Pin_3, S2.Pin_4, U4.GND, C7.-, C6.1, C8.-, IC2.0V, R9.Pin_0, Q2.E, U5.Pin_3, LED4.anode, C14.-, J14.pin1, J14.pin3, R14.Pin_0, D6.anode, C13.-, J12.pin2, J12.pin3, J26.pin1, J28.pin1, J30.pin1, J32.pin1, J34.pin1, J47.pin1
  N6: U2.XLAT1, XTAL2.pin_0, C3.0
  N7: U2.XLAT2, XTAL2.pin_1, C4.0
  N8: U2.D5_(PWM), J39.pin1
  N9: U2.D6_(PWM), J37.pin1
  N10: U2.D7, J36.pin1
  N11: U2.D8, U5.Pin_2, LED3.cathode
  N12: U2.D9_(PWM), Componente3.CE
  N13: U2.D10_(PWM), Componente3.CS
  N14: U2.D11_(PWM), Componente3.MOSI
  N15: U2.D12, Componente3.MISO
  N16: U2.D13, Componente3.SCK
  N17: U2.A0, R14.Pin_1, R15.Pin_0
  N18: U2.A1, J44.pin1
  N19: U2.A2, J45.pin1
  N20: U2.A3, J40.pin1
  N21: U2.A4, IC2.SDA_-_I2C_Data, J24.pin1
  N22: U2.A5, IC2.SCL_-_I2C_Clock, J25.pin1
  N23: BAT2.+, IC2.Vbat_-_Backup_Supply
  N24: Y5.1, IC2.X2_-_Crystal
  N25: Y5.2, IC2.X1_-_Crystal
  N26: Componente3.VCC, U4.output_voltage, C7.+
  N27: R9.Pin_1, LED3.anode
  N28: Q2.B, R10.Pin_1
  N29: Q2.C, D2.anode, OMRON1.COIL1
  N30: R10.Pin_0, U5.Pin_4, R11.Pin_0
  N31: U5.Pin_1, R12.Pin_1
  N32: R11.Pin_1, D2.cathode, J14.pin2, R15.Pin_1, OMRON1.C, OMRON1.COIL2, C13.+, J12.pin1
  N33: LED4.cathode, R13.Pin_1
  N34: J14.pin4, OMRON1.A
  N35: D6.cathode, L5.pin_0, J13.pin1
  N36: L3.pin_0, L4.pin_1
  N37: L5.pin_1, L4.pin_0
