# Fritzing sketch placa completaV2 (saved by Fritzing 0.9.3b)
circuit board: 13.3956cm x 19.6734cm
breadboards: 3

parts:
  U2 = atmega328 [package=dip]
  XTAL2 = Crystal [frequency="16 Mhz" package=THT]
  C3 = Ceramic Capacitor [capacitance=22pF voltage=16V package="100 mil [THT, multilayer]"]
  C4 = Ceramic Capacitor [capacitance=22pF voltage=16V package="100 mil [THT, multilayer]"]
  R2 = Resistor [tolerance=±5% resistance=10k package=THT]
  Componente3 = NRF24L01+ Breakout Board
  S2 = Pushbutton [package="[THT]"]
  U4 = Voltage Regulator - 3.3V [package="TO220 [THT]"]
  C7 = Tantalum Capacitor [capacitance=1μF package="100 mil [THT, tantalum]"]
  C6 = Ceramic Capacitor [capacitance=0.1µF voltage=16V package="100 mil [THT, multilayer]"]
  C8 = Electrolytic Capacitor [capacitance=1μF package="100 mil [THT, electrolytic]"]
  R9 = Resistor [tolerance=±5% resistance=220 package=THT]
  Q2 = NPN-Transistor [package="TO92 [THT]"]
  R10 = Resistor [tolerance=±5% resistance=1k package=THT]
  U5 = Sharp PC817 [package=THT]
  R11 = Resistor [tolerance=±5% resistance=4.7k package=THT]
  R12 = Resistor [tolerance=±5% resistance=330 package=THT]
  LED3 = LED - 5mm [color="Blue (505nm)" package="5 mm [THT]"]
  D2 = Rectifier Diode [part_number=1N4001 package="300 mil [THT]"]
  LED4 = LED - 5mm [color="Green (565nm)" package="5 mm [THT]"]
  R13 = Resistor [tolerance=±5% resistance=220 package=THT]
  C14 = Electrolytic Capacitor [capacitance=1000µF voltage=16V package="200 mil [THT, electrolytic]"]
  D6 = Schottky Diode [part_number=1N5817 package="300 mil [THT]"]
  OMRON1 = OMRON PCB Power Relay – G5LE [part_number="G5LE-1\n" package=THT]
  L3 = Inductor [package="400 mil [THT]"]
  L5 = Inductor [inductance=33µH package="400 mil [THT]"]
  L4 = Inductor [package="400 mil [THT]"]
  C13 = Electrolytic Capacitor [capacitance=100μF package="100 mil [THT, electrolytic]"]
  J21 = female pin header, 1 pin [form="♀ (female)"]  # not connected
  J20 = female pin header, 1 pin [form="♀ (female)"]  # not connected
  Bateria = Camdenboss CTB0158-2 [part_number=CTB0158-2 package=THT]
  Motor = Camdenboss CTB0158-2 [part_number=CTB0158-2 package=THT]
  Controlador = Camdenboss CTB0158-2 [part_number=CTB0158-2 package=THT]
  R14 = Resistor [tolerance=±5% resistance=220 package=THT]
  Q3 = NPN-Transistor [package="TO92 [THT]"]
  R15 = Resistor [tolerance=±5% resistance=1k package=THT]
  U6 = Sharp PC817 [package=THT]
  R16 = Resistor [tolerance=±5% resistance=4.7k package=THT]
  R17 = Resistor [tolerance=±5% resistance=330 package=THT]
  LED5 = LED - 5mm [color="Blue (505nm)" package="5 mm [THT]"]
  D7 = Rectifier Diode [part_number=1N4001 package="300 mil [THT]"]
  OMRON3 = OMRON PCB Power Relay – G5LE [part_number="G5LE-1\n" package=THT]
  R2-1k2 = TRIMPOT [package=3362u-2]
  R4-500 = TRIMPOT [package=3362u-2]
  R3-770 = TRIMPOT [package=3362u-2]
  U7 = LM 358 Dual Op-Amp [package="DIP8 [THT]"]
  R18 = Resistor [tolerance=±5% resistance=100 package=THT]
  NivelR = Camdenboss CTB0158-4 [part_number=CTB0158-4 package=THT]
  servo = Camdenboss CTB0158-3 [part_number=CTB0158-3 package=THT]
  Massa = Camdenboss CTB0158-4 [part_number=CTB0158-4 package=THT]
  tampa = Camdenboss CTB0158-2 [part_number=CTB0158-2 package=THT]
  R19 = Resistor [tolerance=±5% resistance=1k package=THT]
  i2c = Camdenboss CTB0158-4 [part_number=CTB0158-4 package=THT]
  vibra = Camdenboss CTB0158-2 [part_number=CTB0158-2 package=THT]
  J56 = female pin header, 3 pins [form="♀ (female)"]  # not connected
  J55 = female pin header, 2 pins [form="♀ (female)"]  # not connected
  J57 = female pin header, 2 pins [form="♀ (female)"]  # not connected
  J58 = female pin header, 2 pins [form="♀ (female)"]  # not connected
  J59 = female pin header, 2 pins [form="♀ (female)"]  # not connected
  J60 = female pin header, 2 pins [form="♀ (female)"]  # not connected
  J61 = female pin header, 4 pins [form="♀ (female)"]  # not connected
  J62 = female pin header, 4 pins [form="♀ (female)"]  # not connected
  J63 = female pin header, 4 pins [form="♀ (female)"]  # not connected
  J53 = female pin header, 1 pin [form="♀ (female)"]
  J52 = female pin header, 1 pin [form="♀ (female)"]
  J50 = female pin header, 1 pin [form="♀ (female)"]
  J51 = female pin header, 1 pin [form="♀ (female)"]
  J54 = female pin header, 4 pins [form="♀ (female)"]  # not connected
  J64 = female pin header, 4 pins [form="♀ (female)"]  # not connected
  J65 = female pin header, 3 pins [form="♀ (female)"]  # not connected
  J66 = female pin header, 3 pins [form="♀ (female)"]  # not connected
  J67 = female pin header, 3 pins [form="♀ (female)"]  # not connected
  J68 = female pin header, 3 pins [form="♀ (female)"]  # not connected
  J69 = female pin header, 3 pins [form="♀ (female)"]  # not connected
  J70 = female pin header, 2 pins [form="♀ (female)"]  # not connected
  J71 = female pin header, 2 pins [form="♀ (female)"]  # not connected
  J72 = female pin header, 2 pins [form="♀ (female)"]  # not connected
  J73 = female pin header, 2 pins [form="♀ (female)"]  # not connected
  J74 = female pin header, 2 pins [form="♀ (female)"]  # not connected
  J75 = female pin header, 2 pins [form="♀ (female)"]  # not connected
  J76 = female pin header, 2 pins [form="♀ (female)"]  # not connected
  J77 = female pin header, 2 pins [form="♀ (female)"]  # not connected
  J78 = female pin header, 1 pin [form="♀ (female)"]  # not connected
  J79 = female pin header, 1 pin [form="♀ (female)"]  # not connected
  J80 = female pin header, 1 pin [form="♀ (female)"]  # not connected
  J81 = female pin header, 1 pin [form="♀ (female)"]  # not connected
  J82 = female pin header, 1 pin [form="♀ (female)"]  # not connected
  J83 = female pin header, 1 pin [form="♀ (female)"]  # not connected
  J84 = female pin header, 1 pin [form="♀ (female)"]  # not connected
  J85 = female pin header, 1 pin [form="♀ (female)"]  # not connected
  J86 = female pin header, 1 pin [form="♀ (female)"]  # not connected
  J87 = female pin header, 1 pin [form="♀ (female)"]  # not connected
  J88 = female pin header, 1 pin [form="♀ (female)"]  # not connected
  J89 = female pin header, 1 pin [form="♀ (female)"]  # not connected
  J90 = female pin header, 1 pin [form="♀ (female)"]  # not connected
  J91 = female pin header, 1 pin [form="♀ (female)"]  # not connected
  J92 = female pin header, 1 pin [form="♀ (female)"]  # not connected
  J93 = female pin header, 1 pin [form="♀ (female)"]  # not connected
  J94 = female pin header, 1 pin [form="♀ (female)"]  # not connected
  J95 = female pin header, 1 pin [form="♀ (female)"]  # not connected
  J96 = female pin header, 1 pin [form="♀ (female)"]  # not connected
  J97 = female pin header, 1 pin [form="♀ (female)"]  # not connected
  J98 = female pin header, 1 pin [form="♀ (female)"]  # not connected
  J99 = female pin header, 1 pin [form="♀ (female)"]  # not connected
  J100 = female pin header, 1 pin [form="♀ (female)"]  # not connected
  J12 = female pin header, 3 pins [form="♀ (female)"]
  J13 = female pin header, 2 pins [form="♀ (female)"]
  J101 = female pin header, 1 pin [form="♀ (female)"]  # not connected
  J102 = female pin header, 1 pin [form="♀ (female)"]  # not connected
  J103 = female pin header, 1 pin [form="♀ (female)"]  # not connected
  J104 = female pin header, 1 pin [form="♀ (female)"]  # not connected
  J105 = female pin header, 1 pin [form="♀ (female)"]  # not connected
  J106 = female pin header, 1 pin [form="♀ (female)"]  # not connected

nets:
  N1: U2.RESET, R2.Pin_0, S2.Pin_1, S2.Pin_2
  N2: U2.D2, tampa.pin2, R19.Pin_1
  N3: U2.D3_(PWM), Massa.pin2
  N4: U2.D4, Massa.pin3
  N5: U2.VCC, U2.AVCC, R2.Pin_1, U4.input_voltage, C6.0, C8.+, R12.Pin_0, R13.Pin_0, C14.+, L3.pin_1, R17.Pin_0, NivelR.pin4, servo.pin3, Massa.pin4, R19.Pin_0, i2c.pin4, vibra.pin2, J13.pin2
  GND: U2.GND, C3.1, C4.1, Componente3.GND, S2.Pin_3, S2.Pin_4, U4.GND, C7.-, C6.1, C8.-, R9.Pin_0, Q2.E, U5.Pin_3, LED4.anode, C14.-, D6.anode, C13.-, Bateria.pin1, Motor.pin1, Controlador.pin1, R14.Pin_0, Q3.E, U6.Pin_3, R4-500.CCW, U7.connector3, NivelR.pin1, servo.pin1, Massa.pin1, tampa.pin1, i2c.pin1, J12.pin2, J12.pin3
  N6: U2.XLAT1, XTAL2.pin_0, C3.0
  N7: U2.XLAT2, XTAL2.pin_1, C4.0
  N8: U2.D5_(PWM), servo.pin2
  N9: U2.D6_(PWM), NivelR.pin2
  N10: U2.D7, NivelR.pin3
  N11: U2.D8, U5.Pin_2, LED3.cathode
  N12: U2.D9_(PWM), Componente3.CE
  N13: U2.D10_(PWM), Componente3.CS
  N14: U2.D11_(PWM), Componente3.MOSI
  N15: U2.D12, Componente3.MISO
  N16: U2.D13, Componente3.SCK
  N17: U2.A0, U6.Pin_2, LED5.cathode
  N18: U2.A1, R18.Pin_1
  N19: U2.A3, vibra.pin1
  N20: U2.A4, i2c.pin2
  N21: U2.A5, i2c.pin3
  N22: Componente3.VCC, U4.output_voltage, C7.+
  N23: R9.Pin_1, LED3.anode
  N24: Q2.B, R10.Pin_1
  N25: Q2.C, D2.anode, OMRON1.COIL1
  N26: R10.Pin_0, U5.Pin_4, R11.Pin_0
  N27: U5.Pin_1, R12.Pin_1
  N28: R11.Pin_1, D2.cathode, OMRON1.C, OMRON1.COIL2, C13.+, Bateria.pin2, R16.Pin_1, D7.cathode, OMRON3.C, OMRON3.COIL2, J53.pin1, J52.pin1, J50.pin1, J51.pin1, J12.pin1
  N29: LED4.cathode, R13.Pin_1
  N30: D6.cathode, L5.pin_0, J13.pin1
  N31: OMRON1.A, Motor.pin2
  N32: L3.pin_0, L4.pin_1
  N33: L5.pin_1, L4.pin_0
  N34: Controlador.pin2, OMRON3.B
  N35: R14.Pin_1, LED5.anode
  N36: Q3.B, R15.Pin_1
  N37: Q3.C, D7.anode, OMRON3.COIL1
  N38: R15.Pin_0, U6.Pin_4, R16.Pin_0
  N39: U6.Pin_1, R17.Pin_1
  N40: OMRON3.A, R3-770.CCW, U7.connector7
  N41: R2-1k2.CCW, U7.connector5
  N42: R2-1k2.WIPER, U7.connector6, R18.Pin_0
  N43: R4-500.WIPER, R3-770.WIPER, U7.connector4
