# Fritzing sketch teste-nivel ba2t (saved by Fritzing 0.9.3b)
circuit board: 4.11174cm x 2.47136cm
breadboards: 1

parts:
  U1 = LM 358 Dual Op-Amp [package="DIP8 [THT]"]
  R1 = Resistor [tolerance=±5% resistance=1k package=THT]
  R2 = Resistor [tolerance=±5% resistance=1k package=THT]
  R3 = Resistor [tolerance=±5% resistance=470 package=THT]
  R4 = Resistor [tolerance=±5% resistance=330 package=THT]
  R5 = Resistor [tolerance=±5% resistance=100 package=THT]
  R6 = Resistor [tolerance=±5% resistance=1k package=THT]
  R7 = Resistor [tolerance=±5% resistance=220 package=THT]
  J1 = Camdenboss CTB0158-3 [part_number=CTB0158-3 package=THT]

nets:
  N1: U1.connector3, R1.Pin_1, R2.Pin_1, J1.pin3
  N2: U1.connector4, R1.Pin_0, R2.Pin_0, R3.Pin_0
  N3: U1.connector5, R5.Pin_1, R7.Pin_0
  N4: U1.connector6, R6.Pin_1
  N5: U1.connector7, R4.Pin_1, J1.pin1
  N6: R3.Pin_1, R4.Pin_0
  N7: R5.Pin_0, J1.pin2
  N8: R6.Pin_0, R7.Pin_1
